// Logisim project 8_bit_computer.circ as structural Verilog: 2 circuits, main circuit main
module main (
  input  CLR1,
  input  AI,
  input  AO,
  input  ALU_OUT,
  input  SU,
  input  CLRB,
  input  LOAD_INST,
  input  ENABLE_INST,
  input  BI,
  input  B0,
  input  CLR_INST,
  input  D1,
  input  D2,
  input  D3,
  input  D4,
  input  D5,
  input  D6,
  input  D7,
  input  D8,
  input  TST
);

  wire CLK_out, n7486_1_pin1, n7486_1_pin4, n7486_1_pin9, n7486_1_pin12, n74245_1_pin1, n74245_1_pin11,
       n74245_1_pin12, n74245_1_pin13, n74245_1_pin14, n74245_1_pin15, n74245_1_pin16, n74245_1_pin17,
       n74245_1_pin18, n74245_2_pin1, n74245_3_pin1, n74245_4_pin1, n74245_5_pin1, n74245_5_pin2,
       n74245_5_pin3, n74245_5_pin4, n74245_5_pin5, n74245_5_pin6, n74245_5_pin19, n74283_1_pin1,
       n74283_1_pin2, n74283_1_pin3, n74283_1_pin4, n74283_1_pin5, n74283_1_pin6, n74283_1_pin7,
       n74283_1_pin10, n74283_1_pin11, n74283_1_pin12, n74283_1_pin13, n74283_1_pin14, n74283_1_pin15,
       n74283_2_pin1, n74283_2_pin2, n74283_2_pin4, n74283_2_pin6, n74283_2_pin10, n74283_2_pin11,
       n74283_2_pin13, n74283_2_pin15, not_1_out, not_2_out, not_3_out, not_4_out, not_5_out, not_6_out,
       not_7_out, sn74ls173a_2_q1, sn74ls173a_2_q2, sn74ls173a_2_q3, sn74ls173a_2_q4, sn74ls173a_4_q1,
       sn74ls173a_4_q2, sn74ls173a_4_q3, sn74ls173a_4_q4, sn74ls173a_6_q1, sn74ls173a_6_q2, sn74ls173a_6_q3,
       sn74ls173a_6_q4;

  Clock CLK (.out(CLK_out));
  not not_1 (not_1_out, AI);
  not not_2 (not_2_out, AO);
  _74283 u_74283_1 (
    .pin1(n74283_1_pin1), .pin2(n74283_1_pin2), .pin3(n74283_1_pin3), .pin4(n74283_1_pin4),
    .pin5(n74283_1_pin5), .pin6(n74283_1_pin6), .pin7(n74283_1_pin7), .pin15(n74283_1_pin15),
    .pin14(n74283_1_pin14), .pin13(n74283_1_pin13), .pin12(n74283_1_pin12), .pin11(n74283_1_pin11),
    .pin10(n74283_1_pin10));  // open: pin9
  _7486 u_7486_1 (
    .pin1(n7486_1_pin1), .pin2(SU), .pin3(n74283_1_pin11), .pin4(n7486_1_pin4), .pin5(SU),
    .pin6(n74283_1_pin15), .pin13(SU), .pin12(n7486_1_pin12), .pin11(n74283_1_pin6), .pin10(SU),
    .pin9(n7486_1_pin9), .pin8(n74283_1_pin2));
  not not_3 (not_3_out, BI);
  not not_4 (not_4_out, B0);
  SN74LS173A sn74ls173a_1 (
    .D1(n74245_1_pin18), .G1(not_1_out), .G2(not_1_out), .D2(n74245_1_pin17), .CLK(CLK_out), .M(1'b0),
    .D3(n74245_1_pin16), .D4(n74245_1_pin15), .N(1'b0), .CLR(CLR1), .Q1(n74283_1_pin12), .Q2(n74283_1_pin14),
    .Q3(n74283_1_pin3), .Q4(n74283_1_pin5));
  SN74LS173A sn74ls173a_2 (
    .D1(n74245_1_pin14), .G1(not_1_out), .G2(not_1_out), .D2(n74245_1_pin13), .CLK(CLK_out), .M(1'b0),
    .D3(n74245_1_pin12), .D4(n74245_1_pin11), .N(1'b0), .CLR(CLR1), .Q1(sn74ls173a_2_q1),
    .Q2(sn74ls173a_2_q2), .Q3(sn74ls173a_2_q3), .Q4(sn74ls173a_2_q4));
  not not_5 (not_5_out, ALU_OUT);
  LED led_1 (.in(n74283_1_pin10));
  SN74LS173A sn74ls173a_3 (
    .D1(n74245_1_pin18), .G1(not_3_out), .G2(not_3_out), .D2(n74245_1_pin17), .CLK(CLK_out), .M(1'b0),
    .D3(n74245_1_pin16), .D4(n74245_1_pin15), .N(1'b0), .CLR(CLRB), .Q1(n7486_1_pin1), .Q2(n7486_1_pin4),
    .Q3(n7486_1_pin9), .Q4(n7486_1_pin12));
  SN74LS173A sn74ls173a_4 (
    .D1(n74245_1_pin14), .G1(not_3_out), .G2(not_3_out), .D2(n74245_1_pin13), .CLK(CLK_out), .M(1'b0),
    .D3(n74245_1_pin12), .D4(n74245_1_pin11), .N(1'b0), .CLR(CLRB), .Q1(sn74ls173a_4_q1),
    .Q2(sn74ls173a_4_q2), .Q3(sn74ls173a_4_q3), .Q4(sn74ls173a_4_q4));
  LED led_2 (.in(n74283_1_pin12));
  LED led_3 (.in(n74283_1_pin14));
  LED led_4 (.in(n74283_1_pin3));
  LED led_5 (.in(n74283_1_pin5));
  LED led_6 (.in(sn74ls173a_2_q1));
  LED led_7 (.in(sn74ls173a_2_q2));
  LED led_8 (.in(sn74ls173a_2_q3));
  LED led_9 (.in(sn74ls173a_2_q4));
  LED led_10 (.in(n74283_1_pin13));
  LED led_11 (.in(n74283_1_pin1));
  LED led_12 (.in(n74283_1_pin4));
  LED led_13 (.in(n74283_2_pin10));
  LED led_14 (.in(n7486_1_pin1));
  LED led_15 (.in(n7486_1_pin4));
  LED led_16 (.in(n7486_1_pin9));
  LED led_17 (.in(n7486_1_pin12));
  LED led_18 (.in(sn74ls173a_4_q1));
  LED led_19 (.in(sn74ls173a_4_q2));
  LED led_20 (.in(sn74ls173a_4_q3));
  LED led_21 (.in(sn74ls173a_4_q4));
  LED led_22 (.in(n74283_2_pin13));
  LED led_23 (.in(n74283_2_pin1));
  LED led_24 (.in(n74283_2_pin4));
  _74283 u_74283_2 (
    .pin1(n74283_2_pin1), .pin2(n74283_2_pin2), .pin3(sn74ls173a_2_q3), .pin4(n74283_2_pin4),
    .pin5(sn74ls173a_2_q4), .pin6(n74283_2_pin6), .pin7(SU), .pin15(n74283_2_pin15), .pin14(sn74ls173a_2_q2),
    .pin13(n74283_2_pin13), .pin12(sn74ls173a_2_q1), .pin11(n74283_2_pin11), .pin10(n74283_2_pin10),
    .pin9(n74283_1_pin7));
  _74245 u_74245_1 (
    .pin1(n74245_1_pin1), .pin2(n74283_1_pin12), .pin3(n74283_1_pin14), .pin4(n74283_1_pin3),
    .pin5(n74283_1_pin5), .pin6(sn74ls173a_2_q1), .pin7(sn74ls173a_2_q2), .pin8(sn74ls173a_2_q3),
    .pin9(sn74ls173a_2_q4), .pin19(not_2_out), .pin18(n74245_1_pin18), .pin17(n74245_1_pin17),
    .pin16(n74245_1_pin16), .pin15(n74245_1_pin15), .pin14(n74245_1_pin14), .pin13(n74245_1_pin13),
    .pin12(n74245_1_pin12), .pin11(n74245_1_pin11));
  _74245 u_74245_2 (
    .pin1(n74245_2_pin1), .pin2(n74283_1_pin10), .pin3(n74283_1_pin13), .pin4(n74283_1_pin1),
    .pin5(n74283_1_pin4), .pin6(n74283_2_pin10), .pin7(n74283_2_pin13), .pin8(n74283_2_pin1),
    .pin9(n74283_2_pin4), .pin19(not_5_out), .pin18(n74245_1_pin18), .pin17(n74245_1_pin17),
    .pin16(n74245_1_pin16), .pin15(n74245_1_pin15), .pin14(n74245_1_pin14), .pin13(n74245_1_pin13),
    .pin12(n74245_1_pin12), .pin11(n74245_1_pin11));
  _7486 u_7486_2 (
    .pin1(sn74ls173a_4_q1), .pin2(SU), .pin3(n74283_2_pin11), .pin4(sn74ls173a_4_q2), .pin5(SU),
    .pin6(n74283_2_pin15), .pin13(SU), .pin12(sn74ls173a_4_q4), .pin11(n74283_2_pin6), .pin10(SU),
    .pin9(sn74ls173a_4_q3), .pin8(n74283_2_pin2));
  _74245 u_74245_3 (
    .pin1(n74245_3_pin1), .pin2(n7486_1_pin1), .pin3(n7486_1_pin4), .pin4(n7486_1_pin9),
    .pin5(n7486_1_pin12), .pin6(sn74ls173a_4_q1), .pin7(sn74ls173a_4_q2), .pin8(sn74ls173a_4_q3),
    .pin9(sn74ls173a_4_q4), .pin19(not_4_out), .pin18(n74245_1_pin18), .pin17(n74245_1_pin17),
    .pin16(n74245_1_pin16), .pin15(n74245_1_pin15), .pin14(n74245_1_pin14), .pin13(n74245_1_pin13),
    .pin12(n74245_1_pin12), .pin11(n74245_1_pin11));
  not not_6 (not_6_out, TST);
  LED led_25 (.in(n74245_1_pin18));
  LED led_26 (.in(n74245_1_pin17));
  _74245 u_74245_4 (
    .pin1(n74245_4_pin1), .pin2(D1), .pin3(D2), .pin4(D3), .pin5(D4), .pin6(D5), .pin7(D6), .pin8(D7),
    .pin9(D8), .pin19(not_6_out), .pin18(n74245_1_pin18), .pin17(n74245_1_pin17), .pin16(n74245_1_pin16),
    .pin15(n74245_1_pin15), .pin14(n74245_1_pin14), .pin13(n74245_1_pin13), .pin12(n74245_1_pin12),
    .pin11(n74245_1_pin11));
  LED led_27 (.in(n74245_1_pin14));
  LED led_28 (.in(n74245_1_pin13));
  LED led_29 (.in(n74245_1_pin16));
  LED led_30 (.in(n74245_1_pin15));
  LED led_31 (.in(n74245_1_pin12));
  LED led_32 (.in(n74245_1_pin11));
  _74245 u_74245_5 (
    .pin1(n74245_5_pin1), .pin2(n74245_5_pin2), .pin3(n74245_5_pin3), .pin4(n74245_5_pin4),
    .pin5(n74245_5_pin5), .pin6(n74245_5_pin6), .pin7(n74245_5_pin6), .pin8(n74245_5_pin6),
    .pin9(n74245_5_pin6), .pin19(n74245_5_pin19), .pin18(n74245_1_pin11), .pin17(n74245_1_pin12),
    .pin16(n74245_1_pin13), .pin15(n74245_1_pin14), .pin14(n74245_1_pin15), .pin13(n74245_1_pin16),
    .pin12(n74245_1_pin17), .pin11(n74245_1_pin18));
  LED led_33 (.in(sn74ls173a_6_q1));
  LED led_34 (.in(sn74ls173a_6_q2));
  LED led_35 (.in(sn74ls173a_6_q3));
  LED led_36 (.in(sn74ls173a_6_q4));
  LED led_37 (.in(n74245_5_pin5));
  LED led_38 (.in(n74245_5_pin4));
  LED led_39 (.in(n74245_5_pin3));
  LED led_40 (.in(n74245_5_pin2));
  SN74LS173A sn74ls173a_5 (
    .D1(n74245_1_pin14), .G1(not_7_out), .G2(not_7_out), .D2(n74245_1_pin13), .CLK(CLK_out), .M(1'b0),
    .D3(n74245_1_pin12), .D4(n74245_1_pin11), .N(1'b0), .CLR(CLR_INST), .Q1(n74245_5_pin5),
    .Q2(n74245_5_pin4), .Q3(n74245_5_pin3), .Q4(n74245_5_pin2));
  SN74LS173A sn74ls173a_6 (
    .D1(n74245_1_pin18), .G1(not_7_out), .G2(not_7_out), .D2(n74245_1_pin17), .CLK(CLK_out), .M(1'b0),
    .D3(n74245_1_pin16), .D4(n74245_1_pin15), .N(1'b0), .CLR(CLR_INST), .Q1(sn74ls173a_6_q1),
    .Q2(sn74ls173a_6_q2), .Q3(sn74ls173a_6_q3), .Q4(sn74ls173a_6_q4));
  not not_7 (not_7_out, LOAD_INST);
  not not_8 (n74245_5_pin19, ENABLE_INST);
  // also tied to GND on the sheet: n74245_5_pin6
  // also tied to VCC on the sheet: {n74245_2_pin1, n74245_1_pin1, n74245_3_pin1, n74245_4_pin1, n74245_5_pin1}
endmodule

module SN74LS173A (
  input  M,
  input  N,
  input  D1,
  input  G1,
  input  G2,
  input  D2,
  input  CLK,
  input  D3,
  input  D4,
  input  CLR,
  output Q1,
  output Q2,
  output Q3,
  output Q4
);

  wire and_1_out, and_2_out, and_3_out, and_4_out, and_5_out, and_6_out, and_7_out, and_8_out, and_9_out,
       and_10_out, d_ff_1_q, d_ff_1_qn, d_ff_2_q, d_ff_2_qn, d_ff_3_q, d_ff_3_qn, d_ff_4_q, d_ff_4_qn,
       not_1_out, not_2_out, not_3_out, not_4_out, not_5_out, not_6_out, not_7_out, not_8_out, not_9_out,
       not_10_out, not_11_out, not_12_out, not_13_out, not_14_out, not_15_out, or_1_out, or_2_out, or_3_out,
       or_4_out;

  not not_1 (not_1_out, M);
  not not_2 (not_2_out, N);
  not not_3 (not_3_out, G1);
  not not_4 (not_4_out, G2);
  not not_5 (not_5_out, CLK);
  and and_1 (and_1_out, not_1_out, not_2_out);
  and and_2 (and_2_out, not_3_out, not_4_out);
  not not_6 (not_6_out, and_2_out);
  and and_3 (and_3_out, d_ff_1_q, not_6_out);
  and and_4 (and_4_out, D1, and_2_out);
  and and_5 (and_5_out, d_ff_2_q, not_6_out);
  and and_6 (and_6_out, D2, and_2_out);
  and and_7 (and_7_out, d_ff_3_q, not_6_out);
  and and_8 (and_8_out, D3, and_2_out);
  and and_9 (and_9_out, d_ff_4_q, not_6_out);
  and and_10 (and_10_out, D4, and_2_out);
  not not_7 (not_7_out, CLR);
  or or_1 (or_1_out, and_3_out, and_4_out);
  not not_8 (not_8_out, not_7_out);
  or or_2 (or_2_out, and_5_out, and_6_out);
  not not_9 (not_9_out, not_7_out);
  or or_3 (or_3_out, and_7_out, and_8_out);
  not not_10 (not_10_out, not_7_out);
  or or_4 (or_4_out, and_9_out, and_10_out);
  not not_11 (not_11_out, not_7_out);
  D_Flip_Flop d_ff_1 (.D(or_1_out), .clk(not_5_out), .Q(d_ff_1_q), .Qn(d_ff_1_qn), .reset(not_8_out));  // open: preset
  D_Flip_Flop d_ff_2 (.D(or_2_out), .clk(not_5_out), .Q(d_ff_2_q), .Qn(d_ff_2_qn), .reset(not_9_out));  // open: preset
  D_Flip_Flop d_ff_3 (.D(or_3_out), .clk(not_5_out), .Q(d_ff_3_q), .Qn(d_ff_3_qn), .reset(not_10_out));  // open: preset
  D_Flip_Flop d_ff_4 (.D(or_4_out), .clk(not_5_out), .Q(d_ff_4_q), .Qn(d_ff_4_qn), .reset(not_11_out));  // open: preset
  not not_12 (not_12_out, d_ff_1_qn);
  not not_13 (not_13_out, d_ff_2_qn);
  not not_14 (not_14_out, d_ff_3_qn);
  not not_15 (not_15_out, d_ff_4_qn);
  assign Q1 = and_1_out ? not_12_out : 1'bz;  // Controlled_Buffer controlled_buffer_1
  assign Q2 = and_1_out ? not_13_out : 1'bz;  // Controlled_Buffer controlled_buffer_2
  assign Q3 = and_1_out ? not_14_out : 1'bz;  // Controlled_Buffer controlled_buffer_3
  assign Q4 = and_1_out ? not_15_out : 1'bz;  // Controlled_Buffer controlled_buffer_4
endmodule
